# Fritzing sketch esp8266 progrmmer (saved by Fritzing 0.9.3b)
circuit board: 3.93067cm x 3.35697cm
breadboards: 1

parts:
  U1 = ESP8266 WiFi Module [part_number=ESP8266]
  JP1 = FTDI_BASIC [package=ftdi_basic]
  R1 = Resistor [tolerance=±5% resistance=1k package=THT]
  R2 = Resistor [tolerance=±5% resistance=330 package=THT]
  LED1 = LED - 5mm [color="Red (633nm)" package="5 mm [THT]"]
  R3 = Resistor [tolerance=±5% resistance=330 package=THT]
  S1 = Pushbutton [package="[THT]"]
  C1 = Electrolytic Capacitor [capacitance=1µF package="100 mil [THT, electrolytic]"]

nets:
  N1: U1.RXD, JP1.4
  N2: U1.VCC, JP1.3, R2.Pin_0, R3.Pin_0
  N3: U1.GPIO_0, U1.GND, U1.GPIO_15, JP1.1, LED1.cathode, S1.Pin_1, S1.Pin_2, C1.-
  N4: U1.CH_PD, R2.Pin_1
  N5: U1.TXD, JP1.5
  N6: U1.GPIO_16, R1.Pin_0
  N7: U1.REST, R3.Pin_1, S1.Pin_3, S1.Pin_4, C1.+
  N8: R1.Pin_1, LED1.anode
